# Fritzing sketch Scheme (saved by Fritzing 1.0.8)
circuit board: 8.46667cm x 5.64444cm
breadboards: 2

parts:
  ESP32 = MH-ET LIVE ESP32 DEVKIT 38 pins
  R1 = Resistor [tolerance=±5% power=0.25 resistance=1k package=THT]
  Solid_State_Relay = female pin header, 2 pins [form="♀ (female)"]
  D1_1N4001 = Diode [package=diode-hv]
  2N222 = NPN-Transistor [package="TO92 [THT]"]
  black = Pushbutton [package="[THT]"]
  blue = Pushbutton [package="[THT]"]
  red = Pushbutton [package="[THT]"]
  M1 = ESP-Prog [package=THT]
  Thermo_Couple_MAX31855 = Adafruit Thermocouple Amplifier MAX31855 [part_number="Adafruit #269"]
  R2 = Resistor [tolerance=±5% power=0.25W resistance=10k package=THT]
  R3 = Resistor [tolerance=±5% power=0.25W resistance=10k package=THT]
  R4 = Resistor [tolerance=±5% power=0.25W resistance=10k package=THT]
  OLED1 = OLED 1.3" 128x64 I2C SSH1106 (GND/VCC)

nets:
  3V3: ESP32.3V3, Thermo_Couple_MAX31855.VIN, R2.Pin_1, R3.Pin_1, R4.Pin_1
  N1: ESP32.RST, M1.Prog-ESP_EN-.1
  N2: ESP32.IO25, Thermo_Couple_MAX31855.DO
  N3: ESP32.IO26, Thermo_Couple_MAX31855.CS
  N4: ESP32.IO27, Thermo_Couple_MAX31855.CLK
  N5: ESP32.IO14, M1.JTAG-ESP_TMS-.1
  N6: ESP32.IO12, M1.JTAG-ESP_TDI-.1, M1.JTAG-ESP_TDI-1.27
  GND: ESP32.IO13, ESP32.GND#64, 2N222.E, black.Pin_1, black.Pin_2, blue.Pin_1, blue.Pin_2, red.Pin_1, red.Pin_2, M1.JTAG-ESP-TCK-.1, M1.JTAG-GND-5-.1, M1.JTAG-GND-9-.1, M1.Prog-GND-4-.1, M1.JTAG-GND-9-1.27, M1.JTAG-ESP_TCK-1.27, Thermo_Couple_MAX31855.GND, OLED1.GND
  5V: ESP32.5V, Solid_State_Relay.pin2, D1_1N4001.C, OLED1.VCC
  N7: ESP32.IO23, R1.Pin_0
  SCL I2C: ESP32.IO22, OLED1.SCL
  N8: ESP32.TXD0, M1.Prog-ESP_TXD-.1
  N9: ESP32.RXD0, M1.Prog-ESP_RXD-.1
  SDA I2C: ESP32.IO21, OLED1.SDA
  N10: ESP32.IO18, black.Pin_4, R2.Pin_0
  N11: ESP32.IO17, blue.Pin_4, R3.Pin_0
  N12: ESP32.IO16, red.Pin_4, R4.Pin_0
  N13: ESP32.IO15, M1.JAG-ESP-TDO-.1
  N14: R1.Pin_1, 2N222.B
  N15: Solid_State_Relay.pin1, D1_1N4001.A, 2N222.C

notes:
  SSR Connector
  Pull Up resistors

custom parts:
  MH-ET LIVE ESP32 DEVKIT 38 pins: http://mh.nodebb.com/topic/2/mh-et-live-esp32-devkit
  ESP-Prog: Espressif ESP-Prog board. ESP-Prog is one of Espressif’s development and debugging tools, with functions including automatic firmware downloading, serial communication, and JTAG online debugging. ESP-Prog's automatic firmware downloading and serial communication functions are supported on both the ESP8266 and ESP32 platforms, while the JTAG online debugging is supported only on the ESP32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
  Adafruit Thermocouple Amplifier MAX31855: Thermocouples are very sensitive, requiring a good amplifier with a cold-compensation reference. The MAX31855K does everything for you, and can be easily interfaced with any microcontroller, even one without an analog input. This breakout board has the chip itself, a 3.3V regulator with 10uF bypass capacitors and level shifting circuitry, all assembled and tested. Comes with a 2 pin terminal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
  OLED 1.3" 128x64 I2C SSH1106 (GND/VCC): OLED 1.3" 128x64 I2C SSH1106 Pinout: GND/VCC/SCL/SDA
